# Fritzing sketch FritzingScheme (saved by Fritzing 0.9.3b)

parts:
  Componente1 = Arduino Mega 2560 (Rev3)
  R1 = Slide Potentiometer [maximum_resistance=100kΩ]
  LCD1_20x5 = LCD screen  # not connected
  Componente2 = Adafruit I2C+SPI LCD Backpack [part_number="Adafruit #292"]
  KEYPAD1 = Membrane Matrix Keypad
  Componente3 = Arduino Motor Shield

nets:
  N1: Componente1.A8, R1.leg1
  N2: Componente1.D21/SCL, Componente2.CLOCK
  N3: Componente1.D20/SDA, Componente2.DATA
  GND: Componente1.GND, R1.leg2, Componente2.GND
  5V: Componente1.5V, R1.wiper, Componente2.VCC
  N4: Componente1.D22, KEYPAD1.1
  N5: Componente1.D23, KEYPAD1.2
  N6: Componente1.D24, KEYPAD1.3
  N7: Componente1.D25, KEYPAD1.4
  N8: Componente1.D26, KEYPAD1.5
  N9: Componente1.D27, KEYPAD1.7
  N10: Componente1.D28, KEYPAD1.6
  N11: Componente3.D2, Componente3.D13

custom parts:
  LCD screen: A standard character display, usually with 2x16 characters. Comes in many colors.
  Adafruit I2C+SPI LCD Backpack: LCD backpacks reduce the number of pins needed to connect to an LCD. LCDs are a fun and easy way to have your microcontroller project talk back to you. Character LCDs are common, and easy to get, available in tons of colors and sizes. We've written tutorials on using character LCDs with an Arduino (or similar microcontroller) but find that the number of pins necessary to control the LCD can be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
  Membrane Matrix Keypad: Membrane Matrix 3x4 Keypad
